// Logisim project LAB06.circ as structural Verilog: 12 circuits, main circuit main
module main (
  input  in_1,
  input  in_2,
  input  in_3,
  input  in_4,
  input  in_5,
  input  in_6,
  input  in_7,
  output out_8,
  output out_9,
  output out_10,
  output out_11,
  output out_12,
  output [7:0] out_13,
  output [7:0] out_14
);

  and and_1 (out_8, in_1, in_2);
  NAND1 nand1_1 (.in_1(in_1), .in_2(in_2), .out_3(out_9));
  NOR1 nor1_1 (.in_1(in_1), .in_2(in_2), .out_3(out_10));
  MUX21 mux21_1 (.in_1(in_1), .in_2(in_2), .in_3(in_3), .out_4(out_11));
  MUX41 mux41_1 (.in_1(in_1), .in_2(in_2), .in_3(in_4), .in_4(in_5), .in_5(in_6), .in_6(in_7), .out_7(out_12));
  AddMachine addmachine_1 (.out_1(out_13), .out_2(out_14));
endmodule

module NAND1 (
  input  in_1,
  input  in_2,
  output out_3
);

  wire and_1_out;

  and and_1 (and_1_out, in_1, in_2);
  not not_1 (out_3, and_1_out);
endmodule

module NOR1 (
  input  in_1,
  input  in_2,
  output out_3
);

  wire or_1_out;

  or or_1 (or_1_out, in_1, in_2);
  not not_1 (out_3, or_1_out);
endmodule

module MUX21 (
  input  in_1,
  input  in_2,
  input  in_3,
  output out_4
);

  wire and_1_out, and_2_out, not_1_out;

  not not_1 (not_1_out, in_3);
  and and_1 (and_1_out, in_1, not_1_out);
  and and_2 (and_2_out, in_2, in_3);
  or or_1 (out_4, and_1_out, and_2_out);
endmodule

module MUX41 (
  input  in_1,
  input  in_2,
  input  in_3,
  input  in_4,
  input  in_5,
  input  in_6,
  output out_7
);

  wire mux21_1_out_4, mux21_2_out_4;

  MUX21 mux21_1 (.in_1(in_1), .in_2(in_2), .in_3(in_5), .out_4(mux21_1_out_4));
  MUX21 mux21_2 (.in_1(in_3), .in_2(in_4), .in_3(in_5), .out_4(mux21_2_out_4));
  MUX21 mux21_3 (.in_1(mux21_1_out_4), .in_2(mux21_2_out_4), .in_3(in_6), .out_4(out_7));
endmodule

module AddMachine (
  output [7:0] out_1,
  output [7:0] out_2
);

  wire clock_1_out, undriven;

  Adder adder_1 (.a(8'h1), .b(out_2), .out(out_1));  // open: cin, cout
  Register register_1 (.D(out_1), .en(undriven), .clk(clock_1_out), .Q(out_2));  // open: clr
  Clock clock_1 (.out(clock_1_out));
endmodule

module Ex4 (
  input  [7:0] In1,
  output Out1,
  output [7:0] Out2
);

  not not_1 (Out2[7], In1[7]);
  and and_1 (Out1, In1[0], In1[7]);

  assign Out2[6:0] = In1[6:0];
endmodule

module rotr (
  input  [15:0] in_1,
  input  [3:0] in_2,
  output [15:0] out_3
);

  wire [15:0] shiftbyfour_1_out_3, shiftbyone_1_out_3, shiftbytwo_1_out_3;

  ShiftByOne shiftbyone_1 (.in_1(in_1), .in_2(in_2[0]), .out_3(shiftbyone_1_out_3));
  ShiftByTwo shiftbytwo_1 (.in_1(shiftbyone_1_out_3), .in_2(in_2[1]), .out_3(shiftbytwo_1_out_3));
  ShiftByFour shiftbyfour_1 (.in_1(shiftbytwo_1_out_3), .in_2(in_2[2]), .out_3(shiftbyfour_1_out_3));
  ShiftByEight shiftbyeight_1 (.in_1(shiftbyfour_1_out_3), .in_2(in_2[3]), .out_3(out_3));
endmodule

module ShiftByOne (
  input  [15:0] in_1,
  input  in_2,
  output [15:0] out_3
);

  Multiplexer #(.width(16), .enable("false")) multiplexer_1 (
    .in0(in_1), .in1({in_1[0], in_1[15:1]}), .out(out_3), .sel(in_2));
endmodule

module ShiftByTwo (
  input  [15:0] in_1,
  input  in_2,
  output [15:0] out_3
);

  wire [15:0] shiftbyone_1_out_3;

  ShiftByOne shiftbyone_1 (.in_1(in_1), .in_2(in_2), .out_3(shiftbyone_1_out_3));
  ShiftByOne shiftbyone_2 (.in_1(shiftbyone_1_out_3), .in_2(in_2), .out_3(out_3));
endmodule

module ShiftByFour (
  input  [15:0] in_1,
  input  in_2,
  output [15:0] out_3
);

  wire [15:0] shiftbytwo_1_out_3;

  ShiftByTwo shiftbytwo_1 (.in_1(in_1), .in_2(in_2), .out_3(shiftbytwo_1_out_3));
  ShiftByTwo shiftbytwo_2 (.in_1(shiftbytwo_1_out_3), .in_2(in_2), .out_3(out_3));
endmodule

module ShiftByEight (
  input  [15:0] in_1,
  input  in_2,
  output [15:0] out_3
);

  wire [15:0] shiftbyfour_1_out_3;

  ShiftByFour shiftbyfour_1 (.in_1(in_1), .in_2(in_2), .out_3(shiftbyfour_1_out_3));
  ShiftByFour shiftbyfour_2 (.in_1(shiftbyfour_1_out_3), .in_2(in_2), .out_3(out_3));
endmodule
